# Fritzing sketch minimalist_schematic (saved by Fritzing 0.9.3b)
breadboards: 1

parts:
  HC07 = Arduino BT
  Connected_to_Capacitor = Basic Servo
  NANO = Arduino Nano v2.3

nets:
  5V: HC07.5V, Connected_to_Capacitor.vcc, NANO.+5V
  GND: HC07.GND, Connected_to_Capacitor.gnd, NANO.GND
  N1: HC07.RX/D0, NANO.D1TX
  N2: HC07.TX/D1, NANO.D2
  N3: Connected_to_Capacitor.pulse, NANO.D9

notes:
  Vr
  Vf
  Magnetic Loop Bluetooth Remote Control (Alexloop or Homebrew Antenna)
  2014-07-14
  By PU2CLR
