# Fritzing sketch minimalist_schematic_two_capacitors (saved by Fritzing 0.9.3b)
breadboards: 1

parts:
  HC07 = Arduino BT
  Main_Capacitor = Basic Servo
  NANO = Arduino Nano v2.3
  Fine_Tune_Capacitor = Basic Servo

nets:
  5V: HC07.5V, Main_Capacitor.vcc, NANO.+5V, Fine_Tune_Capacitor.vcc
  GND: HC07.GND, Main_Capacitor.gnd, NANO.GND, Fine_Tune_Capacitor.gnd
  N1: HC07.RX/D0, NANO.D1TX
  N2: HC07.TX/D1, NANO.D0RX
  N3: Main_Capacitor.pulse, NANO.D9
  N4: NANO.D8, Fine_Tune_Capacitor.pulse

notes:
  Magnetic Loop Bluetooth Remote Control (Main and fine tune capacitor)
  2014-07-14
  By PU2CLR
